// Logisim project traffic light.circ as structural Verilog: 1 circuit, main circuit main
module main (
  input  in_1,
  output out_2,
  output out_3,
  output out_4,
  output out_5
);

  wire and_1_out, and_2_out, and_3_out, and_4_out, and_5_out, and_6_out, and_7_out, and_8_out, and_9_out,
       and_10_out, and_11_out, and_12_out, and_13_out, and_14_out, and_15_out, clock_1_out, nand_1_out,
       not_1_out, not_2_out, not_3_out, not_4_out, not_5_out, not_6_out, not_7_out, not_8_out, or_1_out,
       or_2_out, or_3_out, t_ff_1_qn, t_ff_2_qn, t_ff_3_qn;

  Clock clock_1 (.out(clock_1_out));
  T_Flip_Flop t_ff_1 (.clk(clock_1_out), .T(in_1), .Q(out_5), .Qn(t_ff_1_qn), .reset(not_1_out));  // open: preset, en
  not not_1 (not_1_out, nand_1_out);
  T_Flip_Flop t_ff_2 (.clk(t_ff_1_qn), .T(in_1), .Q(out_4), .Qn(t_ff_2_qn), .reset(not_2_out));  // open: preset, en
  not not_2 (not_2_out, nand_1_out);
  T_Flip_Flop t_ff_3 (.clk(t_ff_2_qn), .T(in_1), .Q(out_3), .Qn(t_ff_3_qn), .reset(not_3_out));  // open: preset, en
  not not_3 (not_3_out, nand_1_out);
  T_Flip_Flop t_ff_4 (.clk(t_ff_3_qn), .T(in_1), .Q(out_2), .reset(not_4_out));  // open: Qn, preset, en
  not not_4 (not_4_out, nand_1_out);
  nand nand_1 (nand_1_out, out_5, out_4, out_3, out_2);
  not not_5 (not_5_out, out_2);
  not not_6 (not_6_out, out_3);
  not not_7 (not_7_out, out_4);
  not not_8 (not_8_out, out_5);
  and and_1 (and_1_out, out_3, out_5);
  and and_2 (and_2_out, out_3, out_4);
  and and_3 (and_3_out, out_2, not_6_out, not_7_out, not_8_out);
  and and_4 (and_4_out, not_5_out, out_3, out_5);
  and and_5 (and_5_out, not_5_out, out_3, out_4);
  and and_6 (and_6_out, not_5_out, not_7_out, not_8_out);
  and and_7 (and_7_out, not_5_out, not_6_out);
  and and_8 (and_8_out, out_2, out_3);
  and and_9 (and_9_out, out_2, out_4);
  and and_10 (and_10_out, out_2, out_3, not_7_out);
  and and_11 (and_11_out, out_2, not_6_out, out_4);
  and and_12 (and_12_out, not_6_out, not_7_out);
  and and_13 (and_13_out, not_5_out, not_6_out);
  and and_14 (and_14_out, not_5_out, out_3, not_7_out, not_8_out);
  or or_1 (or_1_out, out_2, and_1_out, and_2_out);
  or or_2 (or_2_out, and_3_out, and_4_out, and_5_out);
  and and_15 (and_15_out, out_2, not_6_out, not_7_out, out_5);
  or or_3 (or_3_out, and_6_out, and_8_out, and_9_out);
  // OR_Gate or_4 has open pins: in0=and_10_out, in1=and_11_out, out=open
  // AND_Gate and_16 has open pins: in0=out_2, in1=out_3, in2=out_4, out=open
  // OR_Gate or_5 has open pins: in0=and_12_out, in1=not_5_out, out=open
  LED led_1 (.in(and_13_out));
  LED led_2 (.in(and_14_out));
  LED led_3 (.in(or_1_out));
  LED led_4 (.in(or_2_out));
  LED led_5 (.in(and_15_out));
  LED led_6 (.in(or_3_out));
  LED led_7 ();  // open: in
  LED led_8 ();  // open: in
  LED led_9 ();  // open: in
endmodule
